# Fritzing sketch wiring_diagram (saved by Fritzing 0.9.3b)

parts:
  Part1 = Adafruit DC+Stepper Motor HAT [part_number="Adafruit #2348"]
  M1 = DC Motor
  M3 = DC Motor
  M4 = DC Motor
  M5 = DC Motor
  Part2 = Adafruit DC+Stepper Motor HAT [part_number="Adafruit #2348"]
  M6 = DC Motor
  VCC1 = 4 x AAA Battery Mount
  Raspberry_Pi_1 = Raspberry Pi 3 [part_number=RPI-3-V1.2]  # not connected

nets:
  N1: Part1.M2A, M3.pin_1
  N2: Part1.M2B, M3.pin_2
  N3: Part1.M1B, M1.pin_1
  N4: Part1.M1A, M1.pin_2
  N5: Part1.M4A, M4.pin_1
  N6: Part1.M4B, M4.pin_2
  N7: Part1.M3B, M5.pin_1
  N8: Part1.M3A, M5.pin_2
  N9: Part1.VMOTOR, VCC1.+
  N10: Part2.M3B, M6.pin_1
  N11: Part2.M3A, M6.pin_2
  N12: Part2.GND, VCC1.-

notes:
  (4x) Locomotion Motors
  Writing Tool Motor
  12V Battery Pack
  (2x) Adafruit DC Motor HAT
  Raspberry Pi

custom parts:
  Adafruit DC+Stepper Motor HAT: Let your robotic dreams come true with the new DC+Stepper Motor HAT from Adafruit. This Raspberry Pi add-on is perfect for any motion project as it can drive up to 4 DC or 2 Stepper motors with full PWM speed control. Since the Raspberry Pi does not have a lot of PWM pins, we use a fully-dedicated PWM driver chip onboard to both control motor direction and speed. This chip handles all the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
